# Fritzing sketch schematics (saved by Fritzing 0.9.3b)
circuit board: 6.07583cm x 5.54306cm
breadboards: 1

parts:
  YwRobot_Power_Supply1 = YwRobot Breadboard Power Supply [part_number=545043]
  Part1 = KY-015 Temperature & Humidity Sensor Module [package="Breakout board"]
  R2 = Resistor [tolerance=±5% resistance=10k package=THT]
  U1 = NodeMCU V3.0
  R1 = PHOTOCELL [package=photocell]
  KY-1 = Keyes Relay [package=THT]

nets:
  N1: YwRobot_Power_Supply1.VCC#5, YwRobot_Power_Supply1.VCC#6, U1.Vin, R1.P$1
  N2: YwRobot_Power_Supply1.VCC#9, YwRobot_Power_Supply1.VCC#10, Part1.S, KY-1.signal
  N3: YwRobot_Power_Supply1.GND#11, YwRobot_Power_Supply1.GND#12, R2.Pin_0, U1.GND#6, U1.GND#13, U1.GND#16, U1.GND#33
  N4: YwRobot_Power_Supply1.GND#13, YwRobot_Power_Supply1.GND#14, Part1.-, KY-1.ground
  N5: Part1.Vin, U1.D4
  N6: R2.Pin_1, U1.A0, R1.P$2
  N7: U1.D1, KY-1.power

custom parts:
  YwRobot Breadboard Power Supply: The YwRobot Breadboard Power Supply (MB-V2) has two power rails; they can be 5V or 3V3. Power to the module can be provided through the female USB socket or through the A10 (female) 2.1mm power jack.
  KY-015 Temperature & Humidity Sensor Module: KY-015 temperature and humidity sensor module, provides a low-latency serial interface to measure humidity and temperature.
  NodeMCU V3.0: ESP8266 based NodeMCU
  Keyes Relay: The Keyes 5V relay module is suitable for SCM development, home appliance control. It uses a 5V~12V TIL control signal which can control DC / AC signal.
